// Logisim project Digital_Clock.circ as structural Verilog: 4 circuits, main circuit main
// State register
module main (
);

  wire and_1_out, and_2_out, and_3_out, and_4_out, and_5_out, and_6_out, B1_Deb, B1_out, B2_Deb, B2_out, CK,
       nor_1_out, nor_2_out, not_1_out, not_2_out, or_1_out, or_2_out, or_3_out, RST, undriven;
  wire [1:0] fsm_logic_1_s0_0, State;
  wire [5:0] Hr_q, Min_q, Nr_Hr_q;

  Button B1 (.out(B1_out));
  Button B2 (.out(B2_out));
  Clock u_CK (.out(CK));
  Button u_RST (.out(RST));
  not not_1 (not_1_out, State[0]);
  and and_1 (and_1_out, State[0], State[1]);
  not not_2 (not_2_out, State[1]);
  and and_2 (and_2_out, not_1_out, State[1]);
  and and_3 (and_3_out, State[0], not_2_out);
  nor nor_1 (nor_1_out, not_1_out, State[1]);
  or or_1 (or_1_out, RST, and_3_out, and_4_out);
  or or_2 (or_2_out, RST, nor_1_out, and_5_out);
  Debouncer u_B1_Deb (.CK(CK), .Button_input(B1_out), .O(B1_Deb));  // open: O_INV
  Debouncer u_B2_Deb (.CK(CK), .Button_input(B2_out), .O(B2_Deb));  // open: O_INV
  Time_Reg Min (.INC(B2_Deb), .EN(and_1_out), .RST(or_1_out), .Q(Min_q));
  Time_Reg Hr (.INC(B2_Deb), .EN(and_2_out), .RST(or_2_out), .Q(Hr_q));
  and and_4 (and_4_out, Min_q[5], Min_q[4], Min_q[3], Min_q[2]);
  and and_5 (and_5_out, Hr_q[4], Hr_q[3]);
  FSM_Logic fsm_logic_1 (
    .S1(State[1]), .S0(State[0]), .B1(B1_Deb), .S1_o(fsm_logic_1_s0_0[1]), .S0_0(fsm_logic_1_s0_0[0]));
  nor nor_2 (nor_2_out, State[0], State[1]);
  Register #(.width(2)) State_register (.D(fsm_logic_1_s0_0), .en(1'b1), .clk(CK), .Q(State), .clr(RST));
  or or_3 (or_3_out, and_6_out, RST, nor_2_out);
  Counter #(.max('h3f), .width(6)) Nr_Hr (
    .clr(or_3_out), .clk(undriven), .Q(Nr_Hr_q));  // open: load, up, count, D, carry
  and and_6 (and_6_out, Nr_Hr_q[5], Nr_Hr_q[4], Nr_Hr_q[3], Nr_Hr_q[2]);
endmodule

module FSM_Logic (
  input  S1,
  input  S0,
  input  B1,
  output S1_o,
  output S0_0
);

  wire and_1_out, and_2_out, not_1_out, not_2_out, not_3_out, xor_1_out, xor_2_out, xor_3_out, xor_4_out;

  not not_1 (not_1_out, B1);
  xor xor_1 (xor_1_out, S1, S0);
  not not_2 (not_2_out, S1);
  not not_3 (not_3_out, S0);
  and and_1 (and_1_out, S1, not_1_out);
  and and_2 (and_2_out, xor_1_out, B1);
  xor xor_2 (xor_2_out, B1, not_2_out);
  xor xor_3 (xor_3_out, B1, S0);
  xor xor_4 (xor_4_out, S1, not_3_out);
  or S1_nxt (S1_o, and_1_out, and_2_out);
  or S0_nxt (S0_0, xor_2_out, xor_3_out, xor_4_out);
endmodule

module Debouncer (
  input  CK,
  input  Button_input,
  output O,
  output O_INV
);

  wire and_1_out, and_2_out, d_ff_1_q, d_ff_1_qn, d_ff_2_q, d_ff_2_qn, d_ff_3_q, d_ff_3_qn, not_1_out;

  and and_1 (and_1_out, CK, Button_input);
  D_Flip_Flop d_ff_1 (.D(d_ff_1_qn), .clk(and_1_out), .Q(d_ff_1_q), .Qn(d_ff_1_qn), .reset(not_1_out));  // open: preset
  not not_1 (not_1_out, Button_input);
  D_Flip_Flop d_ff_2 (.D(d_ff_2_qn), .clk(d_ff_1_qn), .Q(d_ff_2_q), .Qn(d_ff_2_qn), .reset(not_1_out));  // open: preset
  D_Flip_Flop d_ff_3 (.D(d_ff_3_qn), .clk(d_ff_2_qn), .Q(d_ff_3_q), .Qn(d_ff_3_qn), .reset(not_1_out));  // open: preset
  and and_2 (and_2_out, d_ff_1_q, d_ff_2_q, d_ff_3_q);
  D_Flip_Flop d_ff_4 (.D(and_2_out), .clk(CK), .Q(O), .Qn(O_INV));  // open: preset, reset
endmodule

module Time_Reg (
  input  INC,
  input  EN,
  input  RST,
  output [5:0] Q
);

  wire and_1_out, d_ff_1_qn, d_ff_2_qn, d_ff_3_qn, d_ff_4_qn, d_ff_5_qn, d_ff_6_qn;

  and and_1 (and_1_out, INC, EN);
  D_Flip_Flop d_ff_1 (.D(d_ff_1_qn), .clk(and_1_out), .Q(Q[0]), .Qn(d_ff_1_qn), .reset(RST));  // open: preset
  D_Flip_Flop d_ff_2 (.D(d_ff_2_qn), .clk(d_ff_1_qn), .Q(Q[1]), .Qn(d_ff_2_qn), .reset(RST));  // open: preset
  D_Flip_Flop d_ff_3 (.D(d_ff_3_qn), .clk(d_ff_2_qn), .Q(Q[2]), .Qn(d_ff_3_qn), .reset(RST));  // open: preset
  D_Flip_Flop d_ff_4 (.D(d_ff_4_qn), .clk(d_ff_3_qn), .Q(Q[3]), .Qn(d_ff_4_qn), .reset(RST));  // open: preset
  D_Flip_Flop d_ff_5 (.D(d_ff_5_qn), .clk(d_ff_4_qn), .Q(Q[4]), .Qn(d_ff_5_qn), .reset(RST));  // open: preset
  D_Flip_Flop d_ff_6 (.D(d_ff_6_qn), .clk(d_ff_5_qn), .Q(Q[5]), .Qn(d_ff_6_qn), .reset(RST));  // open: preset
endmodule
